# Fritzing sketch double garagedoor Arduino (saved by Fritzing 0.9.4)
breadboards: 1

parts:
  WeMos_D1_Mini1 = WeMos D1 Mini
  hc-sr1 = hc-sr04
  hc-sr2 = hc-sr04
  WeMos_D1_Mini_Relay_Shield_V1 = WeMos D1 Mini Relay Shield V2
  U1 = RELAY [package=OJ]

nets:
  VCC: WeMos_D1_Mini1.3V3, hc-sr1.VCC, hc-sr2.VCC
  5V: WeMos_D1_Mini1.5V, WeMos_D1_Mini_Relay_Shield_V1.5V, U1.MAIN
  N1: WeMos_D1_Mini1.D1, WeMos_D1_Mini_Relay_Shield_V1.D1
  GND: WeMos_D1_Mini1.D2, WeMos_D1_Mini1.G, hc-sr1.GND, hc-sr2.GND, WeMos_D1_Mini_Relay_Shield_V1.G, U1.COIL2, U1.COIL1
  N2: WeMos_D1_Mini1.D5, hc-sr2.Echo
  N3: WeMos_D1_Mini1.D6, hc-sr2.Trig
  N4: WeMos_D1_Mini1.D7, hc-sr1.Echo
  N5: WeMos_D1_Mini1.D8, hc-sr1.Trig
